# Fritzing sketch Diagram (saved by Fritzing 0.9.3b)
breadboards: 2

parts:
  S1 = Pushbutton [package="[THT]"]
  R1 = Resistor [tolerance=±5% resistance=1k package="0603 [SMD]"]
  XTAL1 = Crystal [frequency="16 Mhz" package=SMD]
  C2 = Capacitor [package=cap-pth-small-kit]
  C3 = Capacitor [package=cap-pth-small-kit]
  U2 = TEMPERATURE-SENSOR [package=to-92]
  Componente1 = Soil Moisture Sensor
  WeMos_D1_Mini1 = WeMos D1 Mini
  Componente6 = I2C level shifter bidirectional
  R4 = Resistor [tolerance=±5% resistance=4.7k package="0603 [SMD]"]
  Q1 = TRANSISTOR_NPN [package=to-92-ammo]
  R5 = Resistor [tolerance=±5% resistance=1k package="0603 [SMD]"]
  D1 = Rectifier Diode [package="Melf DO-213 AA [SMD]"]
  U3 = RELAY [package=relay-g5q]
  L1 = Solenoid
  U1 = atmega328 [package=dip]

nets:
  N1: S1.Pin_1, S1.Pin_2, R1.Pin_1, U1.RESET
  GND: S1.Pin_3, S1.Pin_4, XTAL1.pin_1, C2.2, C3.2, U2.GND, Componente1.GND, WeMos_D1_Mini1.G, Componente6.GND, Q1.E, L1.pin1, U1.GND
  VCC: R1.Pin_0, U2.VCC, Componente1.VCC, WeMos_D1_Mini1.5V, Componente6.HV, R4.Pin_0, D1.cathode, U3.COIL2, U1.VCC, U1.AVCC
  N2: U2.ADJ, R4.Pin_1
  N3: WeMos_D1_Mini1.3V3, Componente6.LV
  N4: WeMos_D1_Mini1.D1, Componente6.LV1
  N5: WeMos_D1_Mini1.D2, Componente6.LV4
  N6: Q1.B, R5.Pin_1
  N7: Q1.C, D1.anode, U3.COIL1
